// Logisim project LC3-2200a.circ as structural Verilog: 2 circuits, main circuit my circuit
module my_circuit (
);

  wire and_3_out, and_4_out, and_5_out, and_6_out, and_7_out, and_8_out, and_9_out, and_10_out, and_11_out,
       and_12_out, and_13_out, and_14_out, and_15_out, and_16_out, and_17_out, and_18_out, ChkCC, CLK,
       decoder_1_out0, decoder_1_out1, decoder_1_out2, decoder_1_out3, decoder_1_out4, decoder_1_out5,
       decoder_1_out6, decoder_1_out7, decoder_1_out8, decoder_1_out9, decoder_1_out10, decoder_1_out11,
       decoder_1_out12, decoder_1_out13, decoder_1_out14, decoder_1_out15, DrALU, DrMEM, DrOFF, DrPC, DrReg,
       LdA, LdB, LdCC, LdIR, LdMAR, LdPC, not_2_out, OPTest, undriven, undriven_2, undriven_3, undriven_4,
       undriven_5, undriven_6, undriven_7, undriven_8, undriven_9, undriven_10, undriven_11, undriven_12,
       undriven_13, undriven_14, undriven_15, undriven_16, undriven_17, undriven_18, WrMEM, WrReg;
  wire [1:0] AD, CCMatch, func, RegSel;
  wire [2:0] CC_q, comparator_1_gt;
  wire [3:0] RegNo;
  wire [5:0] multiplexer_5_out, rom_1_data, rom_2_data, rom_3_data, State_Register_q;
  wire [23:0] bit_extender_1_out, MAR_q;
  wire [31:0] adder_1_out, and_1_out, and_2_out, bit_extender_2_out, controlled_buffer_1_out, Instruction,
       multiplexer_1_out, multiplexer_2_out, not_1_out, PC_q, ram_1_data, register_3_q, register_4_q,
       register_5_q, register_6_q, register_7_q, register_8_q, register_9_q, register_10_q, register_11_q,
       register_12_q, register_13_q, register_14_q, register_15_q, register_16_q, register_17_q,
       register_18_q, shifter_1_out, shifter_2_out, shifter_3_out, shiftResult, shiftValue, shiftVector;

  Register #(.width(32)) PC (.D(controlled_buffer_1_out), .en(LdPC), .Q(PC_q), .clk(CLK));  // open: clr
  assign controlled_buffer_1_out = DrPC ? PC_q : 32'bz;  // Controlled_Buffer controlled_buffer_1
  Comparator #(.width(32), .mode("unsigned")) comparator_1 (
    .a(controlled_buffer_1_out), .b({32{1'b0}}), .gt(comparator_1_gt[0]), .eq(comparator_1_gt[1]),
    .lt(comparator_1_gt[2]));
  Register #(.width(3)) CC (.D(comparator_1_gt), .en(LdCC), .Q(CC_q));  // open: clk, clr
  assign and_1_out = shiftValue & {shiftVector[31:21], AD, shiftVector[18:0]};  // AND_Gate and_1, 32 bits wide
  Comparator #(.width(3), .mode("unsigned")) comparator_2 (.a(Instruction[23:21]), .b(CC_q));  // open: gt, eq, lt
  assign and_2_out = shiftValue & {shiftVector[31:21], AD, shiftVector[18:0]};  // AND_Gate and_2, 32 bits wide
  assign not_1_out = ~and_2_out;  // NOT_Gate not_1, 32 bits wide
  Multiplexer #(.select(2), .width(32), .disabled(0), .enable("false")) multiplexer_1 (
    .in0(and_1_out), .in1(not_1_out), .in2(adder_1_out), .in3(shiftResult), .out(multiplexer_1_out),
    .sel(func));
  assign controlled_buffer_1_out = DrALU ? multiplexer_1_out : 32'bz;  // Controlled_Buffer controlled_buffer_2
  Register #(.width(32)) register_1 (.D(controlled_buffer_1_out), .en(undriven), .Q(shiftValue));  // open: clk, clr
  Register #(.width(32)) register_2 (
    .D(controlled_buffer_1_out), .en(undriven_2), .Q({shiftVector[31:21], AD, shiftVector[18:0]}));  // open: clk, clr
  Adder #(.width(32)) adder_1 (.a(shiftValue), .b(32'h1), .out(adder_1_out));  // open: cin, cout
  Decoder #(.select(4), .enable("false")) decoder_1 (
    .out0(decoder_1_out0), .out1(decoder_1_out1), .out2(decoder_1_out2), .out3(decoder_1_out3),
    .out4(decoder_1_out4), .out5(decoder_1_out5), .out6(decoder_1_out6), .out7(decoder_1_out7),
    .out8(decoder_1_out8), .out9(decoder_1_out9), .out10(decoder_1_out10), .out11(decoder_1_out11),
    .out12(decoder_1_out12), .out13(decoder_1_out13), .out14(decoder_1_out14), .out15(decoder_1_out15),
    .sel(RegNo));
  and and_3 (and_3_out, decoder_1_out0, WrReg);
  and and_4 (and_4_out, decoder_1_out1, WrReg);
  and and_5 (and_5_out, decoder_1_out2, WrReg);
  and and_6 (and_6_out, decoder_1_out3, WrReg);
  and and_7 (and_7_out, decoder_1_out4, WrReg);
  and and_8 (and_8_out, decoder_1_out5, WrReg);
  and and_9 (and_9_out, decoder_1_out6, WrReg);
  and and_10 (and_10_out, decoder_1_out7, WrReg);
  and and_11 (and_11_out, decoder_1_out8, WrReg);
  and and_12 (and_12_out, decoder_1_out9, WrReg);
  and and_13 (and_13_out, decoder_1_out10, WrReg);
  and and_14 (and_14_out, decoder_1_out11, WrReg);
  and and_15 (and_15_out, decoder_1_out12, WrReg);
  and and_16 (and_16_out, decoder_1_out13, WrReg);
  and and_17 (and_17_out, decoder_1_out14, WrReg);
  and and_18 (and_18_out, decoder_1_out15, WrReg);
  Register #(.width(32)) register_3 (
    .D(controlled_buffer_1_out), .en(and_3_out), .Q(register_3_q), .clk(CLK), .clr(undriven_3));
  Register #(.width(32)) register_4 (
    .D(controlled_buffer_1_out), .en(and_4_out), .Q(register_4_q), .clk(CLK), .clr(undriven_4));
  Register #(.width(32)) register_5 (
    .D(controlled_buffer_1_out), .en(and_5_out), .Q(register_5_q), .clk(CLK), .clr(undriven_5));
  Register #(.width(32)) register_6 (
    .D(controlled_buffer_1_out), .en(and_6_out), .Q(register_6_q), .clk(CLK), .clr(undriven_6));
  Register #(.width(32)) register_7 (
    .D(controlled_buffer_1_out), .en(and_7_out), .Q(register_7_q), .clk(CLK), .clr(undriven_7));
  Register #(.width(32)) register_8 (
    .D(controlled_buffer_1_out), .en(and_8_out), .Q(register_8_q), .clk(CLK), .clr(undriven_8));
  Register #(.width(32)) register_9 (
    .D(controlled_buffer_1_out), .en(and_9_out), .Q(register_9_q), .clk(CLK), .clr(undriven_9));
  Register #(.width(32)) register_10 (
    .D(controlled_buffer_1_out), .en(and_10_out), .Q(register_10_q), .clk(CLK), .clr(undriven_10));
  Register #(.width(32)) register_11 (
    .D(controlled_buffer_1_out), .en(and_11_out), .Q(register_11_q), .clk(CLK), .clr(undriven_11));
  Register #(.width(32)) register_12 (
    .D(controlled_buffer_1_out), .en(and_12_out), .Q(register_12_q), .clk(CLK), .clr(undriven_12));
  Register #(.width(32)) register_13 (
    .D(controlled_buffer_1_out), .en(and_13_out), .Q(register_13_q), .clk(CLK), .clr(undriven_13));
  Register #(.width(32)) register_14 (
    .D(controlled_buffer_1_out), .en(and_14_out), .Q(register_14_q), .clk(CLK), .clr(undriven_14));
  Register #(.width(32)) register_15 (
    .D(controlled_buffer_1_out), .en(and_15_out), .Q(register_15_q), .clk(CLK), .clr(undriven_15));
  Register #(.width(32)) register_16 (
    .D(controlled_buffer_1_out), .en(and_16_out), .Q(register_16_q), .clk(CLK), .clr(undriven_16));
  Register #(.width(32)) register_17 (
    .D(controlled_buffer_1_out), .en(and_17_out), .Q(register_17_q), .clk(CLK), .clr(undriven_17));
  Register #(.width(32)) register_18 (
    .D(controlled_buffer_1_out), .en(and_18_out), .Q(register_18_q), .clk(CLK), .clr(undriven_18));
  Multiplexer #(.select(4), .width(32), .disabled(0), .enable("false")) multiplexer_2 (
    .in0(register_3_q), .in1(register_4_q), .in2(register_5_q), .in3(register_6_q), .in4(register_7_q),
    .in5(register_8_q), .in6(register_9_q), .in7(register_10_q), .in8(register_11_q), .in9(register_12_q),
    .in10(register_13_q), .in11(register_14_q), .in12(register_15_q), .in13(register_16_q),
    .in14(register_17_q), .in15(register_18_q), .out(multiplexer_2_out), .sel(RegNo));
  assign controlled_buffer_1_out = DrReg ? multiplexer_2_out : 32'bz;  // Controlled_Buffer controlled_buffer_3
  Bit_Extender #(.in_width(32), .out_width(24)) bit_extender_1 (.in(controlled_buffer_1_out), .out(bit_extender_1_out));
  Clock clock_1 (.out(CLK));
  Register #(.width(24)) MAR (.D(bit_extender_1_out), .Q(MAR_q));  // open: en, clk, clr
  RAM #(.addrWidth(24), .dataWidth(32), .bus("separate")) ram_1 (
    .addr(MAR_q), .din(controlled_buffer_1_out), .data(ram_1_data), .clk(CLK), .ld(not_2_out));  // open: str, sel, clr
  not not_2 (not_2_out, WrMEM);
  assign controlled_buffer_1_out = DrMEM ? ram_1_data : 32'bz;  // Controlled_Buffer controlled_buffer_4
  Shifter #(.width(32)) shifter_1 (.in(shiftValue), .\dist (shiftVector[4:0]), .out(shifter_1_out));
  Shifter #(.width(32), .shift("lr")) shifter_2 (.in(shiftValue), .\dist (shiftVector[4:0]), .out(shifter_2_out));
  Register #(.width(32)) IR (.D(controlled_buffer_1_out), .en(LdIR), .Q(Instruction), .clk(CLK));  // open: clr
  assign bit_extender_2_out = {{12{1'b0}}, Instruction[19:0]};  // Bit_Extender bit_extender_2
  assign controlled_buffer_1_out = DrOFF ? bit_extender_2_out : 32'bz;  // Controlled_Buffer controlled_buffer_5
  Multiplexer #(.select(2), .width(32), .disabled(0), .enable("false")) multiplexer_3 (
    .in0(shifter_1_out), .in1(shifter_2_out), .in3(shifter_3_out), .out(shiftResult), .sel(AD));  // open: in2
  Shifter #(.width(32), .shift("ar")) shifter_3 (.in(shiftValue), .\dist (shiftVector[4:0]), .out(shifter_3_out));
  Multiplexer #(.select(2), .width(4), .disabled(0), .enable("false")) multiplexer_4 (
    .in0(Instruction[27:24]), .in1(Instruction[23:20]), .in2(Instruction[3:0]), .out(RegNo), .sel(RegSel));  // open: in3
  ROM #(.addrWidth(6), .dataWidth(25)) rom_1 (
    .addr(State_Register_q),
    .data({ChkCC, OPTest, func[0], func[1], RegSel[0], RegSel[1], WrMEM, WrReg, LdCC, LdB, LdA, LdMAR, LdIR, LdPC, DrOFF, DrPC, DrALU, DrMEM, DrReg, rom_1_data}));  // open: sel
  Register #(.width(6)) State_Register (.D(multiplexer_5_out), .Q(State_Register_q), .clk(CLK));  // open: en, clr
  Multiplexer #(.select(2), .width(6), .disabled(0), .enable("false")) multiplexer_5 (
    .in0(rom_1_data), .in1(rom_2_data), .in2(rom_3_data), .out(multiplexer_5_out), .sel({ChkCC, OPTest}));  // open: in3
  ROM #(.addrWidth(4), .dataWidth(6)) rom_2 (
    .addr({Instruction[28], Instruction[29], Instruction[30], Instruction[31]}), .data(rom_2_data));  // open: sel
  ROM #(.addrWidth(2), .dataWidth(6)) rom_3 (.addr(CCMatch), .data(rom_3_data));  // open: sel

  // Other names for the same wires on the sheet: shiftVector[20:19] = AD; IR19_0[19:0] = Instruction[19:0];
  //   OpCode[3:0] = {Instruction[28], Instruction[29], Instruction[30], Instruction[31]}

  // Notes on the sheet:
  //   $zero
  //   $at
  //   $v0
  //   $a1
  //   $a2
  //   $t0
  //   $t1
  //   $t2
  //   $s1
  //   $s2
  //   $k0
  //   $sp
  //   $fp
  //   $ra
  //   contents of rom_1 (hex, n*v repeats v):
  //   6201 1082 e00900 84044 108045 20100 84047 8408 20100 8404a 220100 420c 42010d 80840 8404f 8410 20100
  //   4212 408113 4414 20100 84056 8417 2118 40040 100001a 421b 841c 411d 400900 8405f 8420 8420 620100 21
  //   contents of rom_2 (hex, n*v repeats v):
  //   3 6 19 b e 11 15 1e
  //   contents of rom_3 (hex, n*v repeats v):
  //   0 1a
endmodule

module Registers (
);

  wire undriven, undriven_2, undriven_3, undriven_4, undriven_5, undriven_6, undriven_12, undriven_24,
       undriven_25, undriven_26, undriven_27, undriven_28, undriven_29, undriven_30;
  wire [7:0] register_1_q, register_2_q, register_3_q, register_4_q, register_5_q, register_6_q,
       register_7_q, register_8_q, register_9_q, register_10_q, register_11_q, register_12_q, register_13_q,
       register_14_q, register_15_q, register_16_q, undriven_7, undriven_8, undriven_9, undriven_10,
       undriven_11, undriven_13, undriven_14, undriven_15, undriven_16, undriven_17, undriven_18,
       undriven_19, undriven_20, undriven_21, undriven_22, undriven_23;

  Register register_1 (.D(undriven_7), .en(undriven), .Q(register_1_q), .clk(undriven_24), .clr(undriven_26));
  Register register_2 (.D(undriven_8), .en(undriven_2), .Q(register_2_q), .clk(undriven_25), .clr(undriven_27));
  Register register_3 (.D(undriven_9), .en(undriven_3), .Q(register_3_q), .clr(undriven_28));  // open: clk
  Register register_4 (.D(undriven_10), .en(undriven_4), .Q(register_4_q), .clk(undriven_6), .clr(undriven_29));
  Register register_5 (.D(undriven_11), .en(undriven_5), .Q(register_5_q), .clk(undriven_12), .clr(undriven_30));
  Register register_6 (.D(undriven_13), .Q(register_6_q));  // open: en, clk, clr
  Register register_7 (.D(undriven_14), .Q(register_7_q));  // open: en, clk, clr
  Register register_8 (.D(undriven_15), .Q(register_8_q));  // open: en, clk, clr
  Register register_9 (.D(undriven_16), .Q(register_9_q));  // open: en, clk, clr
  Register register_10 (.D(undriven_17), .Q(register_10_q));  // open: en, clk, clr
  Register register_11 (.D(undriven_18), .Q(register_11_q));  // open: en, clk, clr
  Register register_12 (.D(undriven_19), .Q(register_12_q));  // open: en, clk, clr
  Register register_13 (.D(undriven_20), .Q(register_13_q));  // open: en, clk, clr
  Register register_14 (.D(undriven_21), .Q(register_14_q));  // open: en, clk, clr
  Register register_15 (.D(undriven_22), .Q(register_15_q));  // open: en, clk, clr
  Register register_16 (.D(undriven_23), .Q(register_16_q));  // open: en, clk, clr

  // Notes on the sheet:
  //   $zero
  //   $at
  //   $v0
  //   $a0
  //   $a1
  //   $a2
  //   $t0
  //   $t1
  //   $t2
  //   $s0
  //   $s1
  //   $s2
  //   $k0
  //   $sp
  //   $fp
  //   $ra
endmodule
